# Fritzing sketch NinjaBoard (saved by Fritzing 0.9.2b)
circuit board: 9.65778cm x 6.43268cm
stripboards: 1

parts:
  LEDAmp = ULN2003A [package="DIP16 [THT]"]
  Q1 = Basic FET P-Channel [package="TO220 [THT]"]
  Pulldown_Light_Pin = Resistor [tolerance=±5% resistance=10k package=THT]
  LowpassFilt = Ceramic Capacitor [capacitance=100nF package="100 mil [THT, multilayer]"]
  Sensor3 = Header 4 [package=molex-1x4_lock]
  Sensor2 = Header 4 [package=molex-1x4_lock]
  Sensor1 = Header 4 [package=molex-1x4_lock]
  Temp3 = Header 3 [package=molex-1x3_lock]
  Temp1 = Header 3 [package=molex-1x3_lock]
  Temp2 = Header 3 [package=molex-1x3_lock]
  Arduino_5V = Header 2 [package=molex-1x2_lock]
  Valve = Header 2 [package=molex-1x2_lock]
  Light = Header 2 [package=molex-1x2_lock]
  Led2 = Header 2 [package=molex-1x2_lock]
  Led1 = Header 2 [package=molex-1x2_lock]
  Led2_2 = Header 2 [package=molex-1x2_lock]
  Led2_3 = Header 2 [package=molex-1x2_lock]
  Led1_2 = Header 2 [package=molex-1x2_lock]
  Led1_3 = Header 2 [package=molex-1x2_lock]
  Clock = Header 4 [package=molex-1x4_lock]
  Pullup_Temp_Sensor = Resistor [tolerance=±5% resistance=4.7k package=THT]
  TempArd = female pin header, 1 pin [form="♀ (female)"]
  SensSCL = female pin header, 1 pin [form="♀ (female)"]
  SensSDA = female pin header, 1 pin [form="♀ (female)"]
  LightArd = female pin header, 1 pin [form="♀ (female)"]
  AmpArd = female pin header, 7 pins [form="♀ (female)"]
  12V = Header 2 [package=molex-1x2_lock]

nets:
  N1: LEDAmp.In_1, AmpArd.pin1
  N2: LEDAmp.In_2, AmpArd.pin2
  N3: LEDAmp.In_3, AmpArd.pin3
  N4: LEDAmp.In_4, AmpArd.pin4
  N5: LEDAmp.In_5, AmpArd.pin5
  N6: LEDAmp.In_6, AmpArd.pin6
  N7: LEDAmp.In_7, AmpArd.pin7
  N8: LEDAmp.0V, Q1.source, Pulldown_Light_Pin.Pin_0, Sensor3.1, Sensor2.1, Sensor1.1, Temp3.1, Temp1.1, Temp2.1, Arduino_5V.1, Clock.1, 12V.1
  N9: LEDAmp.COM_-_Common, LowpassFilt.1, Valve.2, Light.2, Led2.2, Led1.2, Led2_2.2, Led2_3.2, Led1_2.2, Led1_3.2, 12V.2
  N10: LEDAmp.Out_7, Valve.1
  N11: LEDAmp.Out_6, Led1.1, Led1_2.1, Led1_3.1
  N12: LEDAmp.Out_5, Led2.1, Led2_2.1, Led2_3.1
  N13: Q1.gate, Pulldown_Light_Pin.Pin_1, LightArd.pin1
  N14: LowpassFilt.0, Light.1
  N15: Sensor3.2, Sensor2.2, Sensor1.2, Clock.2, SensSDA.pin1
  N16: Sensor3.3, Sensor2.3, Sensor1.3, Temp3.3, Temp1.3, Temp2.3, Arduino_5V.2, Clock.3, Pullup_Temp_Sensor.Pin_0
  N17: Sensor3.4, Sensor2.4, Sensor1.4, Clock.4, SensSCL.pin1
  N18: Temp3.2, Temp1.2, Temp2.2, Pullup_Temp_Sensor.Pin_1, TempArd.pin1
